// Logisim project S1-T15_Logisim Simplified.circ as structural Verilog: 14 circuits, main circuit main 2
module Binary_to_Display (
  input  A,
  input  B,
  input  C,
  output a_2,
  output b_2,
  output c_2,
  output d,
  output e,
  output f,
  output g
);

  wire and_1_out, and_2_out, and_3_out, and_4_out, and_5_out, not_1_out, not_2_out, not_3_out, not_4_out,
       or_1_out, or_2_out, or_3_out, xnor_1_out, xnor_2_out, xor_1_out;

  not not_1 (not_1_out, A);
  xnor xnor_1 (xnor_1_out, A, C);
  or u_a (a_2, xnor_1_out, B);
  or u_b (b_2, not_1_out, xnor_2_out);
  or u_c (c_2, xor_1_out, and_1_out);
  or u_d (d, and_3_out, and_4_out);
  and u_e (e, or_2_out, not_4_out);
  xor xor_1 (xor_1_out, A, B);
  or u_f (f, and_2_out, and_5_out);
  not not_2 (not_2_out, B);
  or u_g (g, C, not_2_out, A);
  xnor xnor_2 (xnor_2_out, B, C);
  and and_1 (and_1_out, B, not_4_out);
  not not_3 (not_3_out, xnor_2_out);
  and and_2 (and_2_out, A, not_3_out);
  or or_1 (or_1_out, not_2_out, not_4_out);
  and and_3 (and_3_out, or_1_out, A);
  and and_4 (and_4_out, not_2_out, not_4_out);
  and and_5 (and_5_out, not_1_out, or_3_out);
  or or_2 (or_2_out, not_1_out, B);
  not not_4 (not_4_out, C);
  or or_3 (or_3_out, B, not_4_out);
endmodule

module counter (
  input  Clock,
  input  Enable,
  output A,
  output B,
  output C
);

  wire and_1_out, j_k_ff_1_qn, j_k_ff_2_qn;

  J_K_Flip_Flop j_k_ff_1 (
    .J(1'b1), .clk(Clock), .K(1'b1), .Q(C), .Qn(j_k_ff_1_qn), .preset(and_1_out), .en(Enable));  // open: reset
  J_K_Flip_Flop j_k_ff_2 (
    .J(1'b1), .clk(j_k_ff_1_qn), .K(1'b1), .Q(B), .Qn(j_k_ff_2_qn), .en(Enable), .reset(and_1_out));  // open: preset
  J_K_Flip_Flop j_k_ff_3 (
    .J(1'b1), .clk(j_k_ff_2_qn), .K(1'b1), .Q(A), .en(Enable), .reset(and_1_out));  // open: Qn, preset
  and and_1 (and_1_out, C, B, A);
endmodule

module Fuel_Input (
  input  A,
  input  B,
  input  Plane_detected_in_Radar,
  output High,
  output Normal,
  output Low
);

  wire and_2_out, and_4_out, not_1_out, not_2_out, xor_1_out;

  and and_1 (High, Plane_detected_in_Radar, and_2_out);
  and and_2 (and_2_out, B, A);
  xor xor_1 (xor_1_out, A, B);
  and and_3 (Normal, Plane_detected_in_Radar, xor_1_out);
  not not_1 (not_1_out, B);
  not not_2 (not_2_out, A);
  and and_4 (and_4_out, not_2_out, not_1_out);
  and and_5 (Low, Plane_detected_in_Radar, and_4_out);
endmodule

module BCD_to_Display (
  input  A,
  input  B,
  input  C,
  input  D,
  output a_2,
  output b_2,
  output c_2,
  output d_2,
  output e,
  output f,
  output g
);

  wire and_1_out, and_2_out, and_4_out, not_1_out, not_2_out, not_3_out, or_1_out, or_2_out, or_5_out,
       or_7_out, xnor_1_out, xnor_2_out, xor_1_out, xor_2_out;

  not not_1 (not_1_out, A);
  not not_2 (not_2_out, B);
  not not_3 (not_3_out, C);
  or or_1 (or_1_out, B, not_3_out);
  and and_1 (and_1_out, not_1_out, not_2_out);
  or or_2 (or_2_out, not_2_out, not_1_out);
  and and_2 (and_2_out, B, not_1_out);
  or or_3 (a_2, D, B, xnor_1_out);
  xnor xnor_1 (xnor_1_out, C, A);
  or or_4 (b_2, not_3_out, xnor_2_out);
  xnor xnor_2 (xnor_2_out, B, A);
  and and_3 (e, not_1_out, or_1_out);
  and and_4 (and_4_out, C, or_2_out);
  or or_5 (or_5_out, D, and_2_out);
  xor xor_1 (xor_1_out, C, B);
  or or_6 (g, not_2_out, C, A);
  or or_7 (or_7_out, B, not_1_out);
  or or_8 (d_2, D, and_1_out, and_4_out);
  or or_9 (c_2, or_5_out, xor_1_out);
  xor xor_2 (xor_2_out, C, or_7_out);
  or or_10 (f, or_5_out, xor_2_out);
endmodule

module Timer_to_BCD_12_sec (
  input  Enable,
  input  Clock,
  input  Pulse,
  output Indicator,
  output a,
  output b,
  output b_2,
  output d,
  output e,
  output e_2,
  output g
);

  wire timer_12_final_1_a, timer_12_final_1_b, timer_12_final_1_c, timer_12_final_1_d;

  Timer_12_final timer_12_final_1 (
    .Enable(Enable), .Pulse_Generator(Pulse), .Clock(Clock), .A(timer_12_final_1_a), .B(timer_12_final_1_b),
    .C(timer_12_final_1_c), .D(timer_12_final_1_d), .Indicator(Indicator));
  BCD_to_Display bcd_to_display_1 (
    .A(timer_12_final_1_d), .B(timer_12_final_1_c), .C(timer_12_final_1_b), .D(timer_12_final_1_a), .a_2(a),
    .b_2(b), .c_2(b_2), .d_2(d), .e(e), .f(e_2), .g(g));
  _7_Segment_Display u_7_segment_display_1 (.g(b_2), .f(d), .a(a), .b(b), .e(e), .d(e_2), .c(g));  // open: dp

  // Notes on the sheet:
  //   Timer 12sec
endmodule

module Pulse_gen (
  input  Radar_input,
  input  Radar_input_2,
  input  Clock,
  output Final_Pulse_Generator
);

  wire and_1_out, clock_1_out, d_ff_1_q, d_ff_2_q, or_1_out;

  not not_1 (Final_Pulse_Generator, and_1_out);
  and and_1 (and_1_out, d_ff_1_q, or_1_out);
  Clock clock_1 (.out(clock_1_out));
  D_Flip_Flop d_ff_1 (.clk(clock_1_out), .D(d_ff_2_q), .Q(d_ff_1_q));  // open: Qn, preset, en, reset
  D_Flip_Flop d_ff_2 (.clk(clock_1_out), .D(or_1_out), .Q(d_ff_2_q));  // open: Qn, preset, en, reset
  or or_1 (or_1_out, Radar_input, Radar_input_2);
endmodule

module Timer_12_final (
  input  Enable,
  input  Pulse_Generator,
  input  Clock,
  output A,
  output B,
  output C,
  output D,
  output Indicator
);

  wire and_1_out, and_2_out, not_1_out, not_2_out, not_3_out, not_4_out, not_5_out;

  not not_1 (not_1_out, and_1_out);
  and and_1 (and_1_out, not_2_out, not_3_out, not_4_out, not_5_out);
  and and_2 (and_2_out, Clock, not_1_out);
  J_K_Flip_Flop j_k_ff_1 (
    .J(1'b1), .clk(and_2_out), .K(1'b1), .Q(D), .preset(Pulse_Generator), .en(Enable));  // open: Qn, reset
  and and_3 (Indicator, not_2_out, not_3_out, not_4_out, not_5_out);
  not not_2 (not_2_out, D);
  not not_3 (not_3_out, C);
  not not_4 (not_4_out, B);
  not not_5 (not_5_out, A);
  J_K_Flip_Flop j_k_ff_2 (
    .J(1'b1), .clk(D), .K(1'b1), .Q(C), .en(Enable), .reset(Pulse_Generator));  // open: Qn, preset
  J_K_Flip_Flop j_k_ff_3 (
    .J(1'b1), .clk(C), .K(1'b1), .Q(B), .en(Enable), .reset(Pulse_Generator));  // open: Qn, preset
  J_K_Flip_Flop j_k_ff_4 (
    .J(1'b1), .clk(B), .K(1'b1), .Q(A), .preset(Pulse_Generator), .en(Enable));  // open: Qn, reset
endmodule

module Custom_Comparator (
  input  A,
  input  B,
  input  C,
  output _3,
  output _3_2,
  output _0
);

  wire and_2_out, and_3_out, and_4_out, not_1_out, not_2_out, not_3_out;

  not not_1 (not_1_out, A);
  not not_2 (not_2_out, B);
  not not_3 (not_3_out, C);
  and and_1 (_0, not_1_out, not_2_out, not_3_out);
  and and_2 (and_2_out, not_1_out, C);
  and and_3 (and_3_out, not_1_out, B);
  and and_4 (and_4_out, B, C);
  or or_1 (_3_2, and_2_out, and_3_out, and_4_out);

  assign _3 = A;
endmodule

module runway_checker (
  input  Runway_1_edit,
  input  Clear_Runway_1,
  input  Runway_1_edit_2,
  input  Clear_Runway_2,
  input  Enable,
  output State_of_Runway1,
  output Runway_Availibility,
  output State_of_Runway2
);

  wire R1_qn, R2_qn;

  D_Flip_Flop R1 (
    .clk(Runway_1_edit), .D(R1_qn), .Q(State_of_Runway1), .Qn(R1_qn), .en(Enable), .reset(Clear_Runway_1));  // open: preset
  D_Flip_Flop R2 (
    .clk(Runway_1_edit_2), .D(R2_qn), .Q(State_of_Runway2), .Qn(R2_qn), .en(Enable), .reset(Clear_Runway_2));  // open: preset
  nand nand_1 (Runway_Availibility, State_of_Runway1, State_of_Runway2);

  // Notes on the sheet:
  //   0 - Runway occupied
endmodule

module runway_display (
  input  E,
  input  A,
  input  B,
  output a_2,
  output b_2,
  output c,
  output e_2,
  output f,
  output g,
  output h
);

  wire and_1_out, not_1_out, not_2_out, not_3_out;

  not not_1 (not_1_out, E);
  not not_2 (not_2_out, B);
  not not_3 (not_3_out, A);
  and and_1 (and_1_out, A, B);
  or or_1 (c, not_1_out, B);
  not not_4 (b_2, h);
  or or_2 (h, not_1_out, and_1_out);
  and and_2 (a_2, E, not_3_out, B);
  not not_5 (g, c);

  assign e_2 = a_2;
  assign f = a_2;
endmodule

module main_2 (
  input  Speed,
  input  Range,
  input  Altitude,
  input  Fuel,
  input  in_5,
  input  Emergency,
  input  in_7,
  input  Sensor,
  input  Take_Off_signal,
  input  Gate_Input,
  output out_11,
  output out_12,
  output out_13,
  output out_14,
  output out_15,
  output out_16
);

  wire and_1_out, and_2_out, and_3_out, and_4_out, and_5_out, and_6_out, and_8_out, and_11_out, and_12_out,
       binary_to_display_1_a_2, binary_to_display_1_b_2, binary_to_display_1_c_2, binary_to_display_1_d,
       binary_to_display_1_e, binary_to_display_1_f, binary_to_display_1_g, button_1_out, C_G1_out, C_G2_out,
       C_G3_out, C_G4_out, clock_1_out, clock_2_out, clock_3_out, Clr_R1_out, Clr_R2_out, counter_1_a,
       counter_1_b, counter_1_c, custom_comparator_1__0, custom_comparator_1__3, custom_comparator_1__3_2,
       d_ff_1_q, d_ff_1_qn, d_ff_2_q, d_ff_2_qn, d_ff_3_q, g_to_d_1_a_2, g_to_d_1_b_2, g_to_d_1_c_2,
       g_to_d_1_d_2, g_to_d_1_e, g_to_d_1_f, g_to_d_1_g, g_to_d_1_h, gate_checker_1_state_of_g1,
       gate_checker_1_state_of_g2, gate_checker_1_state_of_g3, gate_checker_1_state_of_g4, not_1_out,
       not_2_out, not_3_out, not_4_out, not_5_out, not_6_out, not_7_out, not_8_out, not_9_out, not_10_out,
       or_1_out, or_2_out, or_3_out, or_5_out, or_6_out, or_7_out, or_8_out, Pulse_from_G1_out,
       Pulse_from_G2_out, Pulse_from_G3_out, Pulse_from_G4_out, pulse_gen_1_final_pulse_generator,
       Runway_1_out, Runway_2_out, runway_checker_1_runway_availibility, runway_display_1_a_2,
       runway_display_1_b_2, runway_display_1_c, runway_display_1_e_2, runway_display_1_f,
       runway_display_1_g, runway_display_1_h, timer_to_bcd_12_sec_1_a, timer_to_bcd_12_sec_1_b,
       timer_to_bcd_12_sec_1_b_2, timer_to_bcd_12_sec_1_d, timer_to_bcd_12_sec_1_e,
       timer_to_bcd_12_sec_1_e_2, timer_to_bcd_12_sec_1_g, timer_to_bcd_12_sec_1_indicator,
       timer_to_bcd_12_sec_2_a, timer_to_bcd_12_sec_2_b, timer_to_bcd_12_sec_2_b_2, timer_to_bcd_12_sec_2_d,
       timer_to_bcd_12_sec_2_e, timer_to_bcd_12_sec_2_e_2, timer_to_bcd_12_sec_2_g,
       timer_to_bcd_12_sec_2_indicator;
  wire [2:0] register_1_q, register_2_q, runway_checker_1_state_of_runway1, sample_1_o1;

  or or_1 (or_1_out, in_7, timer_to_bcd_12_sec_1_indicator);
  not not_1 (not_1_out, in_7);
  Button button_1 (.out(button_1_out));
  _7_Segment_Display u_7_segment_display_1 (
    .g(binary_to_display_1_c_2), .f(binary_to_display_1_d), .a(binary_to_display_1_a_2),
    .b(binary_to_display_1_b_2), .e(binary_to_display_1_e), .d(binary_to_display_1_f),
    .c(binary_to_display_1_g));  // open: dp
  Clock clock_1 (.out(clock_1_out));
  or or_2 (or_2_out, and_2_out, and_12_out);
  counter counter_1 (.Clock(button_1_out), .Enable(Take_Off_signal), .A(counter_1_a), .B(counter_1_b), .C(counter_1_c));
  Binary_to_Display binary_to_display_1 (
    .A(counter_1_a), .B(counter_1_b), .C(counter_1_c), .a_2(binary_to_display_1_a_2),
    .b_2(binary_to_display_1_b_2), .c_2(binary_to_display_1_c_2), .d(binary_to_display_1_d),
    .e(binary_to_display_1_e), .f(binary_to_display_1_f), .g(binary_to_display_1_g));
  and and_1 (and_1_out, Sensor, and_3_out);
  and and_2 (and_2_out, not_1_out, or_3_out);
  Timer_to_BCD_12_sec timer_to_bcd_12_sec_1 (
    .Clock(clock_1_out), .Pulse(pulse_gen_1_final_pulse_generator), .a(timer_to_bcd_12_sec_1_a),
    .b(timer_to_bcd_12_sec_1_b), .b_2(timer_to_bcd_12_sec_1_b_2), .d(timer_to_bcd_12_sec_1_d),
    .e(timer_to_bcd_12_sec_1_e), .e_2(timer_to_bcd_12_sec_1_e_2), .g(timer_to_bcd_12_sec_1_g),
    .Indicator(timer_to_bcd_12_sec_1_indicator), .Enable(or_2_out));
  _7_Segment_Display u_7_segment_display_2 (
    .g(timer_to_bcd_12_sec_1_b_2), .f(timer_to_bcd_12_sec_1_d), .a(timer_to_bcd_12_sec_1_a),
    .b(timer_to_bcd_12_sec_1_b), .e(timer_to_bcd_12_sec_1_e), .d(timer_to_bcd_12_sec_1_e_2),
    .c(timer_to_bcd_12_sec_1_g));  // open: dp
  and and_3 (and_3_out, Speed, Range, Altitude);
  and and_4 (and_4_out, and_1_out, out_12);
  and and_5 (and_5_out, and_1_out, timer_to_bcd_12_sec_2_indicator);
  or or_3 (or_3_out, and_4_out, and_5_out);
  and and_6 (and_6_out, in_7, or_3_out);
  and and_7 (out_14, Gate_Input, or_1_out, counter_1_a);
  not not_2 (not_2_out, out_14);
  not not_3 (not_3_out, Speed);
  LED led_1 (.in(not_3_out));
  and and_8 (and_8_out, or_3_out, timer_to_bcd_12_sec_1_indicator);
  or or_4 (runway_checker_1_state_of_runway1[2], and_6_out, and_8_out);
  Button Runway_1 (.out(Runway_1_out));
  Button Runway_2 (.out(Runway_2_out));
  and and_9 (out_15, Gate_Input, or_1_out, counter_1_b);
  and and_10 (out_16, Gate_Input, or_1_out, counter_1_c);
  not not_4 (not_4_out, out_15);
  not not_5 (not_5_out, out_16);
  and and_11 (and_11_out, not_2_out, not_4_out, not_5_out);
  and and_12 (and_12_out, Gate_Input, and_11_out);
  not not_6 (not_6_out, Altitude);
  not not_7 (not_7_out, Range);
  LED led_2 (.in(not_7_out));
  LED led_3 (.in(not_6_out));
  Button Clr_R1 (.out(Clr_R1_out));
  Clock clock_2 (.out(clock_2_out));
  runway_checker runway_checker_1 (
    .Runway_1_edit(Runway_1_out), .Runway_1_edit_2(Runway_2_out),
    .State_of_Runway1(runway_checker_1_state_of_runway1[0]), .Clear_Runway_1(Clr_R1_out),
    .Runway_Availibility(runway_checker_1_runway_availibility),
    .State_of_Runway2(runway_checker_1_state_of_runway1[1]), .Clear_Runway_2(Clr_R2_out),
    .Enable(runway_checker_1_state_of_runway1[2]));
  Button Clr_R2 (.out(Clr_R2_out));
  Register #(.width(3)) register_1 (
    .D(runway_checker_1_state_of_runway1), .Q(register_1_q), .clk(runway_checker_1_state_of_runway1[2]));  // open: en, clr
  LED led_4 (.in(runway_checker_1_runway_availibility));
  Custom_Comparator custom_comparator_1 (
    .A(out_14), .B(out_15), .C(out_16), ._3(custom_comparator_1__3), ._3_2(custom_comparator_1__3_2),
    ._0(custom_comparator_1__0));
  Timer_to_BCD_12_sec timer_to_bcd_12_sec_2 (
    .Clock(clock_2_out), .Pulse(pulse_gen_1_final_pulse_generator), .a(timer_to_bcd_12_sec_2_a),
    .b(timer_to_bcd_12_sec_2_b), .b_2(timer_to_bcd_12_sec_2_b_2), .d(timer_to_bcd_12_sec_2_d),
    .e(timer_to_bcd_12_sec_2_e), .e_2(timer_to_bcd_12_sec_2_e_2), .g(timer_to_bcd_12_sec_2_g),
    .Indicator(timer_to_bcd_12_sec_2_indicator), .Enable(out_11));
  _7_Segment_Display u_7_segment_display_3 (
    .g(timer_to_bcd_12_sec_2_b_2), .f(timer_to_bcd_12_sec_2_d), .a(timer_to_bcd_12_sec_2_a),
    .b(timer_to_bcd_12_sec_2_b), .e(timer_to_bcd_12_sec_2_e), .d(timer_to_bcd_12_sec_2_e_2),
    .c(timer_to_bcd_12_sec_2_g));  // open: dp
  Clock clock_3 (.out(clock_3_out));
  Pulse_gen pulse_gen_1 (
    .Clock(clock_3_out), .Final_Pulse_Generator(pulse_gen_1_final_pulse_generator), .Radar_input(Sensor),
    .Radar_input_2(Take_Off_signal));
  or or_5 (or_5_out, custom_comparator_1__0, custom_comparator_1__3);
  _7_Segment_Display u_7_segment_display_4 (
    .g(or_5_out), .a(custom_comparator_1__3), .b(or_6_out), .e(custom_comparator_1__3),
    .d(custom_comparator_1__3), .c(custom_comparator_1__3_2), .dp(custom_comparator_1__0));  // open: f
  Fuel_Input fuel_input_1 (
    .Plane_detected_in_Radar(1'b1), .A(Fuel), .B(in_5), .High(out_11), .Normal(out_12), .Low(out_13));
  runway_display runway_display_1 (
    .E(register_1_q[2]), .A(register_1_q[1]), .B(register_1_q[0]), .a_2(runway_display_1_a_2),
    .b_2(runway_display_1_b_2), .c(runway_display_1_c), .e_2(runway_display_1_e_2), .f(runway_display_1_f),
    .g(runway_display_1_g), .h(runway_display_1_h));
  or or_6 (or_6_out, custom_comparator_1__3, custom_comparator_1__3_2);
  or or_7 (or_7_out, out_13, Emergency);
  not not_8 (not_8_out, or_7_out);
  _7_Segment_Display u_7_segment_display_5 (
    .g(not_8_out), .f(or_7_out), .a(or_7_out), .b(or_7_out), .e(or_7_out), .d(or_7_out), .c(or_7_out),
    .dp(not_8_out));
  not not_9 (not_9_out, or_7_out);
  _7_Segment_Display u_7_segment_display_6 (
    .g(not_9_out), .f(or_7_out), .a(or_7_out), .b(or_7_out), .e(or_7_out), .d(or_7_out), .c(or_7_out),
    .dp(not_9_out));
  D_Flip_Flop d_ff_1 (.clk(Runway_1_out), .D(d_ff_1_qn), .Q(d_ff_1_q), .Qn(d_ff_1_qn));  // open: preset, en, reset
  D_Flip_Flop d_ff_2 (.clk(Runway_2_out), .D(d_ff_2_qn), .Q(d_ff_2_q), .Qn(d_ff_2_qn));  // open: preset, en, reset
  LED led_5 (.in(or_7_out));
  _7_Segment_Display u_7_segment_display_7 (
    .g(runway_display_1_c), .a(runway_display_1_a_2), .b(runway_display_1_b_2), .e(runway_display_1_e_2),
    .d(runway_display_1_f), .c(runway_display_1_g), .dp(runway_display_1_h));  // open: f
  Button Pulse_from_G2 (.out(Pulse_from_G2_out));
  or or_8 (or_8_out, d_ff_1_q, d_ff_2_q);
  Button Pulse_from_G3 (.out(Pulse_from_G3_out));
  G_to_D g_to_d_1 (
    .D(1'b0), .C(register_2_q[0]), .B(register_2_q[1]), .A(register_2_q[2]), .a_2(g_to_d_1_a_2),
    .b_2(g_to_d_1_b_2), .c_2(g_to_d_1_c_2), .d_2(g_to_d_1_d_2), .e(g_to_d_1_e), .f(g_to_d_1_f),
    .g(g_to_d_1_g), .h(g_to_d_1_h));
  Button Pulse_from_G1 (.out(Pulse_from_G1_out));
  Button Pulse_from_G4 (.out(Pulse_from_G4_out));
  Button C_G1 (.out(C_G1_out));
  Button C_G2 (.out(C_G2_out));
  _7_Segment_Display u_7_segment_display_8 (
    .g(g_to_d_1_c_2), .f(g_to_d_1_d_2), .a(g_to_d_1_a_2), .b(g_to_d_1_b_2), .e(g_to_d_1_e), .d(g_to_d_1_f),
    .c(g_to_d_1_g), .dp(g_to_d_1_h));
  gate_checker gate_checker_1 (
    .Gate_1_edit(Pulse_from_G1_out), .Gate_2_edit(Pulse_from_G2_out),
    .State_of_G1(gate_checker_1_state_of_g1), .Clear_Gate_1(C_G1_out),
    .State_of_G2(gate_checker_1_state_of_g2), .Clear_Gate_2(C_G2_out), .Gate_3_edit(Pulse_from_G3_out),
    .State_of_G3(gate_checker_1_state_of_g3), .Clear_Gate_3(C_G3_out), .Gate_4_edit(Pulse_from_G4_out),
    .State_of_G4(gate_checker_1_state_of_g4), .Clear_Gate_4(C_G4_out), .Enable(or_8_out));  // open: Gate_Availibility_For_R1, Gate_Availibility_for_R2, Gate_Availibility
  Button C_G3 (.out(C_G3_out));
  Button C_G4 (.out(C_G4_out));
  not not_10 (not_10_out, Sensor);
  sample sample_1 (
    .E(or_8_out), .G1(gate_checker_1_state_of_g1), .G2(gate_checker_1_state_of_g2),
    .G3(gate_checker_1_state_of_g3), .G4(gate_checker_1_state_of_g4), .O1(sample_1_o1[0]),
    .O2(sample_1_o1[1]), .O3(sample_1_o1[2]));
  D_Flip_Flop d_ff_3 (.clk(clock_3_out), .D(or_8_out), .Q(d_ff_3_q), .reset(not_10_out));  // open: Qn, preset, en
  Register #(.width(3)) register_2 (.D(sample_1_o1), .Q(register_2_q), .clk(d_ff_3_q));  // open: en, clr

  // Notes on the sheet:
  //             Weather
  //   MAIN CIRCUIT DIAGRAM
  //   Weather input
  //   Primary
  //   Radar
  //   This is 1 when timer stops
  //   Timer 12 sec, Wait
  //   Once timer stops, weather is okay
  //   T
  //   I
  //   M
  //   E
  //   R
  //   Gate input enabler
  //   Timer 12sec, Wait
  //   Fuel Normal now
  //   RUNWAY CHECKER AND ASSIGNER CIRCUIT
  //   T
  //   I
  //   M
  //   E
  //   R
  //   Input from Radar
  //   Pulse Generator
  //   Runway Allocation
  //   00 - Low Fuel
  //   01 - Adequate Fuel
  //   10 - Adequate Fuel
  //   11 - High Fuel
  //   Fuel Quantity Calc.
  //   Emergency Output
  //   Runway Allocation
  //   Runway 0
  //   Filled
  //   Gate 0
  //   Ground Vehicles
  //   Dispatched
  //   Instructions
  //   and Gates 4,5,6 are in terminal 2, next to runway 2
  //   1) Give the data in the radar first to implement landing
  //   2) Turn on take off signal first to implement the take off
  //   TEAM ID: T15
  //   Himanshu Singh Patel, 231CS127
  //   Nishant Kumar, 231CS140
  //   R Adithya, 231CS146
  //   Gate Allocation
  //   GATE CHECKER AND ASSIGNER CIRCUIT
  //   Note that Gates 1,2,3 are in Terminal 1, next to runway 1.
  //   3) The speed, range and altitude must reach an optimum level before the runway gets assigned
  //   REAL TIME AIR TRAFFIC CONTROL SYSTEM
  //   in case its not an emergency. Once its made optimum, the runway is assigned depending on other factors
endmodule

module gate_checker (
  input  Gate_1_edit,
  input  Clear_Gate_1,
  input  Gate_2_edit,
  input  Clear_Gate_2,
  input  Gate_3_edit,
  input  Clear_Gate_3,
  input  Gate_4_edit,
  input  Clear_Gate_4,
  input  Enable,
  output State_of_G1,
  output Gate_Availibility_For_R1,
  output State_of_G2,
  output Gate_Availibility,
  output State_of_G3,
  output Gate_Availibility_for_R2,
  output State_of_G4
);

  wire G1_qn, G2_qn, G3_qn, G4_qn;

  D_Flip_Flop G1 (
    .clk(Gate_1_edit), .D(G1_qn), .Q(State_of_G1), .Qn(G1_qn), .en(Enable), .reset(Clear_Gate_1));  // open: preset
  D_Flip_Flop G2 (
    .clk(Gate_2_edit), .D(G2_qn), .Q(State_of_G2), .Qn(G2_qn), .en(Enable), .reset(Clear_Gate_2));  // open: preset
  D_Flip_Flop G3 (
    .clk(Gate_3_edit), .D(G3_qn), .Q(State_of_G3), .Qn(G3_qn), .en(Enable), .reset(Clear_Gate_3));  // open: preset
  D_Flip_Flop G4 (
    .clk(Gate_4_edit), .D(G4_qn), .Q(State_of_G4), .Qn(G4_qn), .en(Enable), .reset(Clear_Gate_4));  // open: preset
  nand nand_1 (Gate_Availibility_For_R1, State_of_G1, State_of_G2);
  nand nand_2 (Gate_Availibility_for_R2, State_of_G3, State_of_G4);
  or or_1 (Gate_Availibility, Gate_Availibility_For_R1, Gate_Availibility_for_R2);

  // Notes on the sheet:
  //   0 - Gate occupied
  //   0 - Gate occupied
endmodule

module sample (
  input  E,
  input  G1,
  input  G2,
  input  G3,
  input  G4,
  output O1,
  output O2,
  output O3
);

  wire and_1_out, and_2_out, and_3_out, and_4_out, and_5_out, not_1_out, not_2_out, not_3_out, not_4_out,
       not_5_out, not_6_out, not_7_out;

  not not_1 (not_1_out, E);
  and and_1 (and_1_out, G1, G2, G3);
  not not_2 (not_2_out, G2);
  not not_3 (not_3_out, G3);
  not not_4 (not_4_out, G3);
  or or_1 (O1, not_1_out, and_1_out);
  not not_5 (not_5_out, E);
  and and_2 (and_2_out, G1, not_2_out);
  and and_3 (and_3_out, G1, not_3_out);
  not not_6 (not_6_out, E);
  not not_7 (not_7_out, G1);
  and and_4 (and_4_out, G2, not_4_out);
  and and_5 (and_5_out, G2, G4);
  or or_2 (O2, not_5_out, and_2_out, and_3_out);
  or or_3 (O3, not_6_out, not_7_out, and_4_out, and_5_out);
endmodule

module G_to_D (
  input  D,
  input  C,
  input  B,
  input  A,
  output a_2,
  output b_2,
  output c_2,
  output d_2,
  output e,
  output f,
  output g,
  output h
);

  wire and_1_out, and_2_out, and_5_out, and_6_out, and_7_out, and_8_out, not_1_out, not_2_out, not_3_out,
       not_4_out, not_5_out, not_6_out, not_7_out, not_8_out, not_9_out, not_10_out, not_11_out, not_12_out,
       not_13_out, not_14_out, not_15_out;

  not not_1 (not_1_out, C);
  and and_1 (and_1_out, not_1_out, not_2_out);
  not not_2 (not_2_out, A);
  not not_3 (not_3_out, C);
  and and_2 (and_2_out, not_3_out, B);
  not not_4 (not_4_out, C);
  or or_1 (b_2, not_4_out, not_5_out);
  not not_5 (not_5_out, A);
  or or_2 (c_2, B, C);
  not not_6 (not_6_out, B);
  and and_3 (d_2, not_6_out, not_7_out);
  not not_7 (not_7_out, A);
  not not_8 (not_8_out, C);
  and and_4 (e, not_8_out, not_9_out);
  not not_9 (not_9_out, A);
  not not_10 (not_10_out, C);
  and and_5 (and_5_out, not_10_out, not_11_out);
  not not_11 (not_11_out, A);
  not not_12 (not_12_out, C);
  and and_6 (and_6_out, not_12_out, B);
  not not_13 (not_13_out, B);
  and and_7 (and_7_out, not_13_out, not_14_out);
  not not_14 (not_14_out, A);
  not not_15 (not_15_out, C);
  and and_8 (and_8_out, not_15_out, A);
  and and_9 (h, C, A);
  or or_3 (a_2, and_1_out, and_2_out);
  or or_4 (f, and_5_out, and_6_out);
  or or_5 (g, and_7_out, and_8_out);
endmodule
