// Logisim project S1-T15_Logisim.circ as structural Verilog: 17 circuits, main circuit Main Circuit RTATC
module Binary_to_Display (
  input  A,
  input  B,
  input  C,
  output a_2,
  output b_2,
  output c_2,
  output d,
  output e,
  output f,
  output g
);

  wire and_1_out, and_2_out, and_3_out, and_4_out, and_5_out, not_1_out, not_2_out, not_3_out, not_4_out,
       or_1_out, or_2_out, or_3_out, xnor_1_out, xnor_2_out, xor_1_out;

  not not_1 (not_1_out, A);
  xnor xnor_1 (xnor_1_out, A, C);
  or u_a (a_2, xnor_1_out, B);
  or u_b (b_2, not_1_out, xnor_2_out);
  or u_c (c_2, xor_1_out, and_1_out);
  or u_d (d, and_3_out, and_4_out);
  and u_e (e, or_2_out, not_4_out);
  xor xor_1 (xor_1_out, A, B);
  or u_f (f, and_2_out, and_5_out);
  not not_2 (not_2_out, B);
  or u_g (g, C, not_2_out, A);
  xnor xnor_2 (xnor_2_out, B, C);
  and and_1 (and_1_out, B, not_4_out);
  not not_3 (not_3_out, xnor_2_out);
  and and_2 (and_2_out, A, not_3_out);
  or or_1 (or_1_out, not_2_out, not_4_out);
  and and_3 (and_3_out, or_1_out, A);
  and and_4 (and_4_out, not_2_out, not_4_out);
  and and_5 (and_5_out, not_1_out, or_3_out);
  or or_2 (or_2_out, not_1_out, B);
  not not_4 (not_4_out, C);
  or or_3 (or_3_out, B, not_4_out);
endmodule

module counter (
  input  Clock,
  input  in_2,
  output A,
  output B,
  output C
);

  wire and_1_out, j_k_ff_1_qn, j_k_ff_2_qn;

  J_K_Flip_Flop j_k_ff_1 (
    .J(1'b1), .clk(Clock), .K(1'b1), .Q(C), .Qn(j_k_ff_1_qn), .preset(and_1_out), .en(in_2));  // open: reset
  J_K_Flip_Flop j_k_ff_2 (
    .J(1'b1), .clk(j_k_ff_1_qn), .K(1'b1), .Q(B), .Qn(j_k_ff_2_qn), .en(in_2), .reset(and_1_out));  // open: preset
  J_K_Flip_Flop j_k_ff_3 (
    .J(1'b1), .clk(j_k_ff_2_qn), .K(1'b1), .Q(A), .en(in_2), .reset(and_1_out));  // open: Qn, preset
  and and_1 (and_1_out, C, B, A);
endmodule

module MVC (
  input  A,
  input  B,
  input  C,
  output o
);

  wire and_1_out, and_2_out, and_3_out;

  and and_1 (and_1_out, A, B);
  and and_2 (and_2_out, B, C);
  and and_3 (and_3_out, A, C);
  or or_1 (o, and_1_out, and_2_out, and_3_out);
endmodule

module Gate_input_full (
  output A,
  output B,
  output C
);

  wire a_out, and_1_out, and_2_out, and_3_out, and_4_out, and_5_out, and_6_out, b_out, button_1_out, c_out,
       d_out, e_out, f_out, g_out, j_k_ff_1_qn, j_k_ff_2_qn, not_1_out, not_2_out, not_3_out, not_4_out,
       or_1_out, or_2_out, or_3_out, xnor_1_out, xnor_2_out, xor_1_out;

  _7_Segment_Display u_7_segment_display_1 (
    .g(c_out), .f(d_out), .a(a_out), .b(b_out), .e(e_out), .d(f_out), .c(g_out));  // open: dp
  not not_1 (not_1_out, A);
  xnor xnor_1 (xnor_1_out, A, C);
  or u_a (a_out, xnor_1_out, B);
  or u_b (b_out, not_1_out, xnor_2_out);
  or u_c (c_out, xor_1_out, and_2_out);
  or d (d_out, and_3_out, and_4_out);
  and e (e_out, or_2_out, not_4_out);
  Button button_1 (.out(button_1_out));
  xor xor_1 (xor_1_out, A, B);
  or f (f_out, and_1_out, and_5_out);
  J_K_Flip_Flop j_k_ff_1 (
    .J(1'b1), .clk(button_1_out), .K(1'b1), .Q(C), .Qn(j_k_ff_1_qn), .reset(and_6_out));  // open: preset, en
  not not_2 (not_2_out, B);
  xnor xnor_2 (xnor_2_out, B, C);
  not not_3 (not_3_out, xnor_2_out);
  and and_1 (and_1_out, A, not_3_out);
  or g (g_out, C, not_2_out, A);
  J_K_Flip_Flop j_k_ff_2 (
    .J(1'b1), .clk(j_k_ff_1_qn), .K(1'b1), .Q(B), .Qn(j_k_ff_2_qn), .reset(and_6_out));  // open: preset, en
  and and_2 (and_2_out, B, not_4_out);
  J_K_Flip_Flop j_k_ff_3 (.J(1'b1), .clk(j_k_ff_2_qn), .K(1'b1), .Q(A), .reset(and_6_out));  // open: Qn, preset, en
  or or_1 (or_1_out, not_2_out, not_4_out);
  and and_3 (and_3_out, or_1_out, A);
  and and_4 (and_4_out, not_2_out, not_4_out);
  and and_5 (and_5_out, not_1_out, or_3_out);
  and and_6 (and_6_out, C, B, A);
  not not_4 (not_4_out, C);
  or or_2 (or_2_out, not_1_out, B);
  or or_3 (or_3_out, B, not_4_out);
endmodule

module Fuel_Input (
  input  A,
  input  B,
  input  Plane_detected_in_Radar,
  output High,
  output Normal,
  output Low
);

  wire and_2_out, and_4_out, not_1_out, not_2_out, xor_1_out;

  and and_1 (High, Plane_detected_in_Radar, and_2_out);
  and and_2 (and_2_out, B, A);
  xor xor_1 (xor_1_out, A, B);
  and and_3 (Normal, Plane_detected_in_Radar, xor_1_out);
  not not_1 (not_1_out, B);
  not not_2 (not_2_out, A);
  and and_4 (and_4_out, not_2_out, not_1_out);
  and and_5 (Low, Plane_detected_in_Radar, and_4_out);
endmodule

module Plane_Input (
  input  S1,
  input  S2,
  input  S3,
  input  R1,
  input  R2,
  input  R3,
  input  A1,
  input  A2,
  input  A3,
  input  Plane_detected_in_Radar,
  output S,
  output R,
  output A
);

  wire mvc_1_o, mvc_2_o, mvc_3_o;

  MVC mvc_1 (.A(S3), .B(S2), .C(S1), .o(mvc_1_o));
  and and_1 (S, Plane_detected_in_Radar, mvc_1_o);
  MVC mvc_2 (.A(R3), .B(R2), .C(R1), .o(mvc_2_o));
  and and_2 (R, Plane_detected_in_Radar, mvc_2_o);
  MVC mvc_3 (.A(A3), .B(A2), .C(A1), .o(mvc_3_o));
  and and_3 (A, Plane_detected_in_Radar, mvc_3_o);

  // Notes on the sheet:
  //   Speed
  //                  Range
  //                         Altitude
endmodule

module Binary_to_BCD (
  input  A,
  input  B,
  input  C,
  input  D,
  output B4,
  output B3,
  output B2,
  output B1,
  output B0
);

  wire and_2_out, and_3_out, not_1_out, not_2_out, not_3_out, or_1_out, or_2_out;

  not not_1 (not_1_out, A);
  not not_2 (not_2_out, C);
  not not_3 (not_3_out, B);
  or or_1 (or_1_out, B, C);
  and and_1 (B3, A, not_3_out, not_2_out);
  or or_2 (or_2_out, not_1_out, C);
  and and_2 (and_2_out, not_1_out, C);
  and and_3 (and_3_out, A, B, not_2_out);
  and and_4 (B4, A, or_1_out);
  and and_5 (B2, B, or_2_out);
  or or_3 (B1, and_2_out, and_3_out);

  assign B0 = D;
endmodule

module BCD_to_Display (
  input  A,
  input  B,
  input  C,
  input  D,
  output a_2,
  output b_2,
  output c_2,
  output d_2,
  output e,
  output f,
  output g
);

  wire and_1_out, and_2_out, and_4_out, not_1_out, not_2_out, not_3_out, or_1_out, or_2_out, or_5_out,
       or_7_out, xnor_1_out, xnor_2_out, xor_1_out, xor_2_out;

  not not_1 (not_1_out, A);
  not not_2 (not_2_out, B);
  not not_3 (not_3_out, C);
  or or_1 (or_1_out, B, not_3_out);
  and and_1 (and_1_out, not_1_out, not_2_out);
  or or_2 (or_2_out, not_2_out, not_1_out);
  and and_2 (and_2_out, B, not_1_out);
  or or_3 (a_2, D, B, xnor_1_out);
  xnor xnor_1 (xnor_1_out, C, A);
  or or_4 (b_2, not_3_out, xnor_2_out);
  xnor xnor_2 (xnor_2_out, B, A);
  and and_3 (e, not_1_out, or_1_out);
  and and_4 (and_4_out, C, or_2_out);
  or or_5 (or_5_out, D, and_2_out);
  xor xor_1 (xor_1_out, C, B);
  or or_6 (g, not_2_out, C, A);
  or or_7 (or_7_out, B, not_1_out);
  or or_8 (d_2, D, and_1_out, and_4_out);
  or or_9 (c_2, or_5_out, xor_1_out);
  xor xor_2 (xor_2_out, C, or_7_out);
  or or_10 (f, or_5_out, xor_2_out);
endmodule

module Timer_to_BCD_15_sec (
  input  Enable,
  input  clock,
  input  Pulse,
  output Indicator,
  output a,
  output b,
  output c,
  output d,
  output e,
  output f,
  output g,
  output a_2,
  output b_2,
  output c_2,
  output d_2,
  output e_2,
  output f_2,
  output g_2,
  output Pulse_2
);

  wire binary_to_bcd_1_b0, binary_to_bcd_1_b1, binary_to_bcd_1_b2, binary_to_bcd_1_b3, binary_to_bcd_1_b4,
       not_1_out, not_2_out, not_3_out, not_4_out, timer_15_final_1_a, timer_15_final_1_b,
       timer_15_final_1_c, timer_15_final_1_d;

  not not_1 (not_1_out, timer_15_final_1_c);
  not not_2 (not_2_out, timer_15_final_1_d);
  not not_3 (not_3_out, timer_15_final_1_a);
  not not_4 (not_4_out, timer_15_final_1_b);
  and and_1 (Pulse_2, not_2_out, not_1_out, not_4_out, not_3_out);
  Timer_15_final timer_15_final_1 (
    .Enable(Enable), .Pulse_Generator(Pulse), .Clock(clock), .A(timer_15_final_1_a), .B(timer_15_final_1_b),
    .C(timer_15_final_1_c), .D(timer_15_final_1_d), .Indicator(Indicator));
  Binary_to_BCD binary_to_bcd_1 (
    .A(timer_15_final_1_a), .B(timer_15_final_1_b), .C(timer_15_final_1_c), .D(timer_15_final_1_d),
    .B4(binary_to_bcd_1_b4), .B3(binary_to_bcd_1_b3), .B2(binary_to_bcd_1_b2), .B1(binary_to_bcd_1_b1),
    .B0(binary_to_bcd_1_b0));
  BCD_to_Display bcd_to_display_1 (
    .A(binary_to_bcd_1_b4), .B(1'b0), .C(1'b0), .D(1'b0), .a_2(a), .b_2(b), .c_2(c), .d_2(d), .e(e), .f(f),
    .g(g));
  BCD_to_Display bcd_to_display_2 (
    .A(binary_to_bcd_1_b0), .B(binary_to_bcd_1_b1), .C(binary_to_bcd_1_b2), .D(binary_to_bcd_1_b3),
    .a_2(a_2), .b_2(b_2), .c_2(c_2), .d_2(d_2), .e(e_2), .f(f_2), .g(g_2));
  _7_Segment_Display u_7_segment_display_1 (.g(c_2), .f(d_2), .a(a_2), .b(b_2), .e(e_2), .d(f_2), .c(g_2));  // open: dp
  _7_Segment_Display u_7_segment_display_2 (.g(c), .f(d), .a(a), .b(b), .e(e), .d(f), .c(g));  // open: dp

  // Notes on the sheet:
  //   Timer 15sec
endmodule

module Timer_to_BCD_12_sec (
  input  Enable,
  input  Clock,
  input  Pulse,
  output Indicator,
  output a,
  output b,
  output b_2,
  output d,
  output e,
  output e_2,
  output g,
  output a_2,
  output b_3,
  output b_4,
  output d_2,
  output e_3,
  output e_4,
  output g_2
);

  wire binary_to_bcd_1_b0, binary_to_bcd_1_b1, binary_to_bcd_1_b2, binary_to_bcd_1_b3, binary_to_bcd_1_b4,
       timer_12_final_1_a, timer_12_final_1_b, timer_12_final_1_c, timer_12_final_1_d;

  Timer_12_final timer_12_final_1 (
    .Enable(Enable), .Pulse_Generator(Pulse), .Clock(Clock), .A(timer_12_final_1_a), .B(timer_12_final_1_b),
    .C(timer_12_final_1_c), .D(timer_12_final_1_d), .Indicator(Indicator));
  Binary_to_BCD binary_to_bcd_1 (
    .A(timer_12_final_1_a), .B(timer_12_final_1_b), .C(timer_12_final_1_c), .D(timer_12_final_1_d),
    .B4(binary_to_bcd_1_b4), .B3(binary_to_bcd_1_b3), .B2(binary_to_bcd_1_b2), .B1(binary_to_bcd_1_b1),
    .B0(binary_to_bcd_1_b0));
  BCD_to_Display bcd_to_display_1 (
    .A(binary_to_bcd_1_b4), .B(1'b0), .C(1'b0), .D(1'b0), .a_2(a), .b_2(b), .c_2(b_2), .d_2(d), .e(e),
    .f(e_2), .g(g));
  BCD_to_Display bcd_to_display_2 (
    .A(binary_to_bcd_1_b0), .B(binary_to_bcd_1_b1), .C(binary_to_bcd_1_b2), .D(binary_to_bcd_1_b3),
    .a_2(a_2), .b_2(b_3), .c_2(b_4), .d_2(d_2), .e(e_3), .f(e_4), .g(g_2));
  _7_Segment_Display u_7_segment_display_1 (.g(b_2), .f(d), .a(a), .b(b), .e(e), .d(e_2), .c(g));  // open: dp
  _7_Segment_Display u_7_segment_display_2 (.g(b_4), .f(d_2), .a(a_2), .b(b_3), .e(e_3), .d(e_4), .c(g_2));  // open: dp

  // Notes on the sheet:
  //   Timer 12sec
endmodule

module Radar_Input (
  input  A,
  input  B,
  input  C,
  output P,
  output Q,
  output R
);

  wire xor_1_out;

  MVC mvc_1 (.A(C), .B(B), .C(A), .o(Q));
  xor xor_1 (xor_1_out, C, B);
  xor xor_2 (R, xor_1_out, A);

  assign P = 1'b0;
endmodule

module Main_Circuit_RTATC (
  input  Speed,
  input  in_2,
  input  in_3,
  input  Range,
  input  in_5,
  input  in_6,
  input  Altitude,
  input  in_8,
  input  in_9,
  input  Fuel,
  input  in_11,
  input  Emergency,
  input  in_13,
  input  in_14,
  input  Sensor,
  input  Sensor_2,
  input  in_17,
  input  Take_Off_signal,
  input  in_19,
  output out_20,
  output out_21,
  output out_22,
  output out_23,
  output out_24,
  output out_25,
  output out_26,
  output [2:0] out_27
);

  wire Altitude_out, and_1_out, and_2_out, and_3_out, and_4_out, and_5_out, and_6_out, and_9_out, and_10_out,
       and_11_out, and_16_out, and_17_out, and_18_out, and_19_out, and_20_out, binary_to_display_1_a_2,
       binary_to_display_1_b_2, binary_to_display_1_c_2, binary_to_display_1_d, binary_to_display_1_e,
       binary_to_display_1_f, binary_to_display_1_g, button_1_out, CLEAR_2_out, CLEAR_out, clock_1_out,
       clock_2_out, clock_3_out, clock_4_out, counter_1_a, counter_1_b, counter_1_c, custom_comparator_1__0,
       custom_comparator_1__3, custom_comparator_1__3_2, gate_to_display_1_a_2, gate_to_display_1_b_2,
       gate_to_display_1_c_2, gate_to_display_1_d_2, gate_to_display_1_e, gate_to_display_1_f,
       gate_to_display_1_g, not_1_out, not_2_out, not_3_out, not_4_out, not_5_out, not_6_out, not_7_out,
       not_8_out, not_9_out, not_10_out, not_11_out, not_12_out, not_13_out, or_1_out, or_2_out, or_3_out,
       or_4_out, or_5_out, or_6_out, or_7_out, or_8_out, or_9_out, or_10_out, or_11_out, or_12_out,
       or_13_out, plane_input_1_a, plane_input_1_r, plane_input_1_s, pulse_gen_1_final_pulse_generator,
       pulse_gen_2_final_pulse_generator, radar_input_1_p, radar_input_1_q, radar_input_1_r, Range_out,
       Speed_out, t_ff_1_q, t_ff_1_qn, t_ff_2_q, t_ff_3_q, t_ff_3_qn, t_ff_4_q, t_ff_5_q, t_ff_5_qn,
       t_ff_6_q, timer_to_bcd_12_sec_1_a, timer_to_bcd_12_sec_1_a_2, timer_to_bcd_12_sec_1_b,
       timer_to_bcd_12_sec_1_b_2, timer_to_bcd_12_sec_1_b_3, timer_to_bcd_12_sec_1_b_4,
       timer_to_bcd_12_sec_1_d, timer_to_bcd_12_sec_1_d_2, timer_to_bcd_12_sec_1_e,
       timer_to_bcd_12_sec_1_e_2, timer_to_bcd_12_sec_1_e_3, timer_to_bcd_12_sec_1_e_4,
       timer_to_bcd_12_sec_1_g, timer_to_bcd_12_sec_1_g_2, timer_to_bcd_12_sec_1_indicator,
       timer_to_bcd_12_sec_2_a, timer_to_bcd_12_sec_2_a_2, timer_to_bcd_12_sec_2_b,
       timer_to_bcd_12_sec_2_b_2, timer_to_bcd_12_sec_2_b_3, timer_to_bcd_12_sec_2_b_4,
       timer_to_bcd_12_sec_2_d, timer_to_bcd_12_sec_2_d_2, timer_to_bcd_12_sec_2_e,
       timer_to_bcd_12_sec_2_e_2, timer_to_bcd_12_sec_2_e_3, timer_to_bcd_12_sec_2_e_4,
       timer_to_bcd_12_sec_2_g, timer_to_bcd_12_sec_2_g_2, timer_to_bcd_12_sec_2_indicator,
       timer_to_bcd_12_sec_3_a, timer_to_bcd_12_sec_3_a_2, timer_to_bcd_12_sec_3_b,
       timer_to_bcd_12_sec_3_b_2, timer_to_bcd_12_sec_3_b_3, timer_to_bcd_12_sec_3_b_4,
       timer_to_bcd_12_sec_3_d, timer_to_bcd_12_sec_3_d_2, timer_to_bcd_12_sec_3_e,
       timer_to_bcd_12_sec_3_e_2, timer_to_bcd_12_sec_3_e_3, timer_to_bcd_12_sec_3_e_4,
       timer_to_bcd_12_sec_3_g, timer_to_bcd_12_sec_3_g_2, timer_to_bcd_12_sec_3_indicator,
       timer_to_bcd_12_sec_4_indicator;
  wire [2:0] and_15_out;

  MVC mvc_1 (.A(in_14), .B(or_1_out), .C(in_13), .o(out_20));
  or or_1 (or_1_out, timer_to_bcd_12_sec_1_indicator, timer_to_bcd_12_sec_2_indicator);
  or or_2 (or_2_out, out_20, timer_to_bcd_12_sec_2_indicator);
  Radar_Input radar_input_1 (
    .A(Sensor), .B(Sensor_2), .C(in_17), .P(radar_input_1_p), .Q(radar_input_1_q), .R(radar_input_1_r));
  not not_1 (not_1_out, out_20);
  _7_Segment_Display u_7_segment_display_1 (
    .g(timer_to_bcd_12_sec_1_b_2), .f(timer_to_bcd_12_sec_1_d), .a(timer_to_bcd_12_sec_1_a),
    .b(timer_to_bcd_12_sec_1_b), .e(timer_to_bcd_12_sec_1_e), .d(timer_to_bcd_12_sec_1_e_2),
    .c(timer_to_bcd_12_sec_1_g));  // open: dp
  Button button_1 (.out(button_1_out));
  _7_Segment_Display u_7_segment_display_2 (
    .g(binary_to_display_1_c_2), .f(binary_to_display_1_d), .a(binary_to_display_1_a_2),
    .b(binary_to_display_1_b_2), .e(binary_to_display_1_e), .d(binary_to_display_1_f),
    .c(binary_to_display_1_g));  // open: dp
  or or_3 (or_3_out, radar_input_1_p, radar_input_1_q, radar_input_1_r);
  Clock clock_1 (.out(clock_1_out));
  counter counter_1 (.Clock(button_1_out), .in_2(Take_Off_signal), .A(counter_1_a), .B(counter_1_b), .C(counter_1_c));
  Binary_to_Display binary_to_display_1 (
    .A(counter_1_a), .B(counter_1_b), .C(counter_1_c), .a_2(binary_to_display_1_a_2),
    .b_2(binary_to_display_1_b_2), .c_2(binary_to_display_1_c_2), .d(binary_to_display_1_d),
    .e(binary_to_display_1_e), .f(binary_to_display_1_f), .g(binary_to_display_1_g));
  Plane_Input plane_input_1 (
    .Plane_detected_in_Radar(or_3_out), .S1(Speed), .S2(in_2), .S3(in_3), .R1(Range), .R2(in_5), .R3(in_6),
    .A1(Altitude), .A2(in_8), .A3(in_9), .S(plane_input_1_s), .R(plane_input_1_r), .A(plane_input_1_a));
  and and_1 (and_1_out, not_1_out, or_4_out);
  Timer_to_BCD_12_sec timer_to_bcd_12_sec_1 (
    .Clock(clock_1_out), .Pulse(pulse_gen_1_final_pulse_generator), .a(timer_to_bcd_12_sec_1_a),
    .a_2(timer_to_bcd_12_sec_1_a_2), .b(timer_to_bcd_12_sec_1_b), .b_3(timer_to_bcd_12_sec_1_b_3),
    .b_2(timer_to_bcd_12_sec_1_b_2), .b_4(timer_to_bcd_12_sec_1_b_4), .d(timer_to_bcd_12_sec_1_d),
    .d_2(timer_to_bcd_12_sec_1_d_2), .e(timer_to_bcd_12_sec_1_e), .e_3(timer_to_bcd_12_sec_1_e_3),
    .e_2(timer_to_bcd_12_sec_1_e_2), .e_4(timer_to_bcd_12_sec_1_e_4), .g(timer_to_bcd_12_sec_1_g),
    .g_2(timer_to_bcd_12_sec_1_g_2), .Indicator(timer_to_bcd_12_sec_1_indicator), .Enable(and_1_out));
  _7_Segment_Display u_7_segment_display_3 (
    .g(timer_to_bcd_12_sec_1_b_4), .f(timer_to_bcd_12_sec_1_d_2), .a(timer_to_bcd_12_sec_1_a_2),
    .b(timer_to_bcd_12_sec_1_b_3), .e(timer_to_bcd_12_sec_1_e_3), .d(timer_to_bcd_12_sec_1_e_4),
    .c(timer_to_bcd_12_sec_1_g_2));  // open: dp
  _7_Segment_Display u_7_segment_display_4 (
    .g(timer_to_bcd_12_sec_2_b_2), .f(timer_to_bcd_12_sec_2_d), .a(timer_to_bcd_12_sec_2_a),
    .b(timer_to_bcd_12_sec_2_b), .e(timer_to_bcd_12_sec_2_e), .d(timer_to_bcd_12_sec_2_e_2),
    .c(timer_to_bcd_12_sec_2_g));  // open: dp
  and and_2 (and_2_out, plane_input_1_s, plane_input_1_r, plane_input_1_a);
  not not_2 (not_2_out, and_2_out);
  and and_3 (and_3_out, and_2_out, timer_to_bcd_12_sec_3_indicator);
  and and_4 (and_4_out, and_2_out, out_22);
  or or_4 (or_4_out, and_4_out, and_3_out);
  and and_5 (and_5_out, out_20, or_4_out);
  and and_6 (and_6_out, or_3_out, not_12_out);
  Button CLEAR (.out(CLEAR_out));
  and and_7 (out_24, in_19, counter_1_a);
  and and_8 (and_15_out[2], or_2_out, out_24);
  not not_3 (not_3_out, and_15_out[2]);
  and and_9 (and_9_out, in_19, and_16_out);
  Clock clock_2 (.out(clock_2_out));
  not not_4 (not_4_out, plane_input_1_s);
  and u_Speed (Speed_out, not_2_out, not_4_out);
  and u_Range (Range_out, not_2_out, not_7_out);
  LED led_1 (.in(Speed_out));
  LED led_2 (.in(Range_out));
  and and_10 (and_10_out, or_4_out, timer_to_bcd_12_sec_1_indicator);
  or or_5 (or_5_out, and_5_out, and_10_out);
  and and_11 (and_11_out, and_6_out, or_5_out);
  or or_6 (or_6_out, and_17_out, and_18_out, CLEAR_out, or_11_out);
  and and_12 (out_26, in_19, counter_1_c);
  and and_13 (out_25, in_19, counter_1_b);
  and and_14 (and_15_out[1], or_2_out, out_25);
  and and_15 (and_15_out[0], or_2_out, out_26);
  not not_5 (not_5_out, and_15_out[0]);
  not not_6 (not_6_out, and_15_out[1]);
  and and_16 (and_16_out, not_3_out, not_6_out, not_5_out);
  Timer_to_BCD_12_sec timer_to_bcd_12_sec_2 (
    .Clock(clock_2_out), .Pulse(pulse_gen_2_final_pulse_generator), .a(timer_to_bcd_12_sec_2_a),
    .a_2(timer_to_bcd_12_sec_2_a_2), .b(timer_to_bcd_12_sec_2_b), .b_3(timer_to_bcd_12_sec_2_b_3),
    .b_2(timer_to_bcd_12_sec_2_b_2), .b_4(timer_to_bcd_12_sec_2_b_4), .d(timer_to_bcd_12_sec_2_d),
    .d_2(timer_to_bcd_12_sec_2_d_2), .e(timer_to_bcd_12_sec_2_e), .e_3(timer_to_bcd_12_sec_2_e_3),
    .e_2(timer_to_bcd_12_sec_2_e_2), .e_4(timer_to_bcd_12_sec_2_e_4), .g(timer_to_bcd_12_sec_2_g),
    .g_2(timer_to_bcd_12_sec_2_g_2), .Indicator(timer_to_bcd_12_sec_2_indicator), .Enable(and_9_out));
  _7_Segment_Display u_7_segment_display_5 (
    .g(timer_to_bcd_12_sec_2_b_4), .f(timer_to_bcd_12_sec_2_d_2), .a(timer_to_bcd_12_sec_2_a_2),
    .b(timer_to_bcd_12_sec_2_b_3), .e(timer_to_bcd_12_sec_2_e_3), .d(timer_to_bcd_12_sec_2_e_4),
    .c(timer_to_bcd_12_sec_2_g_2));  // open: dp
  not not_7 (not_7_out, plane_input_1_r);
  not not_8 (not_8_out, plane_input_1_a);
  and u_Altitude (Altitude_out, not_2_out, not_8_out);
  LED led_3 (.in(Altitude_out));
  T_Flip_Flop t_ff_1 (.clk(and_11_out), .T(1'b1), .Q(t_ff_1_q), .Qn(t_ff_1_qn), .reset(or_6_out));  // open: preset, en
  Clock clock_3 (.out(clock_3_out));
  T_Flip_Flop t_ff_2 (.clk(t_ff_1_qn), .T(1'b1), .Q(t_ff_2_q), .reset(or_6_out));  // open: Qn, preset, en
  and and_17 (and_17_out, t_ff_1_q, t_ff_2_q);
  _7_Segment_Display u_7_segment_display_6 (
    .g(timer_to_bcd_12_sec_3_b_2), .f(timer_to_bcd_12_sec_3_d), .a(timer_to_bcd_12_sec_3_a),
    .b(timer_to_bcd_12_sec_3_b), .e(timer_to_bcd_12_sec_3_e), .d(timer_to_bcd_12_sec_3_e_2),
    .c(timer_to_bcd_12_sec_3_g));  // open: dp
  Timer_to_BCD_12_sec timer_to_bcd_12_sec_3 (
    .Clock(clock_3_out), .Pulse(pulse_gen_1_final_pulse_generator), .a(timer_to_bcd_12_sec_3_a),
    .a_2(timer_to_bcd_12_sec_3_a_2), .b(timer_to_bcd_12_sec_3_b), .b_3(timer_to_bcd_12_sec_3_b_3),
    .b_2(timer_to_bcd_12_sec_3_b_2), .b_4(timer_to_bcd_12_sec_3_b_4), .d(timer_to_bcd_12_sec_3_d),
    .d_2(timer_to_bcd_12_sec_3_d_2), .e(timer_to_bcd_12_sec_3_e), .e_3(timer_to_bcd_12_sec_3_e_3),
    .e_2(timer_to_bcd_12_sec_3_e_2), .e_4(timer_to_bcd_12_sec_3_e_4), .g(timer_to_bcd_12_sec_3_g),
    .g_2(timer_to_bcd_12_sec_3_g_2), .Indicator(timer_to_bcd_12_sec_3_indicator), .Enable(out_21));
  _7_Segment_Display u_7_segment_display_7 (
    .g(timer_to_bcd_12_sec_3_b_4), .f(timer_to_bcd_12_sec_3_d_2), .a(timer_to_bcd_12_sec_3_a_2),
    .b(timer_to_bcd_12_sec_3_b_3), .e(timer_to_bcd_12_sec_3_e_3), .d(timer_to_bcd_12_sec_3_e_4),
    .c(timer_to_bcd_12_sec_3_g_2));  // open: dp
  and and_18 (and_18_out, t_ff_2_q, t_ff_1_qn);
  Clock clock_4 (.out(clock_4_out));
  Pulse_gen pulse_gen_1 (
    .Clock(clock_4_out), .Final_Pulse_Generator(pulse_gen_1_final_pulse_generator), .Radar_input(or_3_out),
    .Radar_input_2(or_3_out));
  Pulse_gen pulse_gen_2 (
    .Clock(clock_4_out), .Final_Pulse_Generator(pulse_gen_2_final_pulse_generator),
    .Radar_input(Take_Off_signal), .Radar_input_2(Take_Off_signal));
  Register #(.width(3)) register_1 (.D(and_15_out), .Q(out_27), .clk(clock_2_out));  // open: en, clr
  Fuel_Input fuel_input_1 (
    .Plane_detected_in_Radar(or_3_out), .A(Fuel), .B(in_11), .High(out_21), .Normal(out_22), .Low(out_23));
  Custom_Comparator custom_comparator_1 (
    .A(out_27[2]), .B(out_27[1]), .C(out_27[0]), ._3(custom_comparator_1__3),
    ._3_2(custom_comparator_1__3_2), ._0(custom_comparator_1__0));
  or or_7 (or_7_out, out_23, Emergency);
  not not_9 (not_9_out, or_7_out);
  _7_Segment_Display u_7_segment_display_8 (
    .g(not_9_out), .f(or_7_out), .a(or_7_out), .b(or_7_out), .e(or_7_out), .d(or_7_out), .c(or_7_out),
    .dp(not_9_out));
  not not_10 (not_10_out, or_7_out);
  _7_Segment_Display u_7_segment_display_9 (
    .g(not_10_out), .f(or_7_out), .a(or_7_out), .b(or_7_out), .e(or_7_out), .d(or_7_out), .c(or_7_out),
    .dp(not_10_out));
  not not_11 (not_11_out, t_ff_1_q);
  LED led_4 (.in(or_7_out));
  not not_12 (not_12_out, and_19_out);
  T_Flip_Flop t_ff_3 (.clk(t_ff_1_q), .T(1'b1), .Q(t_ff_3_q), .Qn(t_ff_3_qn), .reset(or_11_out));  // open: preset, en
  T_Flip_Flop t_ff_4 (.clk(t_ff_3_qn), .T(1'b1), .Q(t_ff_4_q), .reset(or_11_out));  // open: Qn, preset, en
  Gate_to_Display gate_to_display_1 (
    .A(t_ff_3_q), .B(t_ff_4_q), .C(t_ff_5_q), .D(t_ff_6_q), .a_2(gate_to_display_1_a_2),
    .b_2(gate_to_display_1_b_2), .c_2(gate_to_display_1_c_2), .d_2(gate_to_display_1_d_2),
    .e(gate_to_display_1_e), .f(gate_to_display_1_f), .g(gate_to_display_1_g));
  not not_13 (not_13_out, t_ff_1_q);
  or or_8 (or_8_out, not_13_out, and_20_out);
  and and_19 (and_19_out, t_ff_3_q, t_ff_4_q, t_ff_5_q, t_ff_6_q);
  _7_Segment_Display u_7_segment_display_10 (
    .g(or_8_out), .a(and_20_out), .b(or_9_out), .e(and_20_out), .d(and_20_out), .c(t_ff_1_q));  // open: f, dp
  Timer_to_BCD_12_sec timer_to_bcd_12_sec_4 (
    .Clock(clock_3_out), .Pulse(pulse_gen_1_final_pulse_generator),
    .Indicator(timer_to_bcd_12_sec_4_indicator), .Enable(and_19_out));  // open: a, a_2, b, b_3, b_2, b_4, d, d_2, e, e_3, e_2, e_4, g, g_2
  T_Flip_Flop t_ff_5 (.clk(t_ff_2_q), .T(1'b1), .Q(t_ff_5_q), .Qn(t_ff_5_qn), .reset(or_11_out));  // open: preset, en
  and and_20 (and_20_out, not_11_out, or_10_out);
  _7_Segment_Display u_7_segment_display_11 (
    .g(gate_to_display_1_c_2), .f(gate_to_display_1_d_2), .a(gate_to_display_1_a_2),
    .b(gate_to_display_1_b_2), .e(gate_to_display_1_g), .d(gate_to_display_1_f), .c(gate_to_display_1_e));  // open: dp
  or or_9 (or_9_out, t_ff_1_q, and_20_out);
  T_Flip_Flop t_ff_6 (.clk(t_ff_5_qn), .T(1'b1), .Q(t_ff_6_q), .reset(or_11_out));  // open: Qn, preset, en
  or or_10 (or_10_out, t_ff_5_q, t_ff_6_q);
  or or_11 (or_11_out, timer_to_bcd_12_sec_4_indicator, CLEAR_2_out);
  Button CLEAR_2 (.out(CLEAR_2_out));
  or or_12 (or_12_out, custom_comparator_1__0, custom_comparator_1__3);
  _7_Segment_Display u_7_segment_display_12 (
    .g(or_12_out), .a(custom_comparator_1__3), .b(or_13_out), .e(custom_comparator_1__3),
    .d(custom_comparator_1__3), .c(custom_comparator_1__3_2), .dp(custom_comparator_1__0));  // open: f
  or or_13 (or_13_out, custom_comparator_1__3, custom_comparator_1__3_2);

  // Notes on the sheet:
  //             Weather
  //   MAIN CIRCUIT DIAGRAM
  //   Weather input
  //   Secondary 
  //   Primary
  //   Radar
  //   Radar
  //   Radar
  //   This is 1 when timer stops
  //   Timer 12 sec, Wait
  //   Once timer stops, weather is okay
  //   T
  //   I
  //   M
  //   E
  //   R
  //   Once timer stops, weather is okay
  //   This is 1 when timer stops
  //   Gate Input
  //   This can only be used to disable and enable the timer with the help of AND or OR gate
  //   MVC for inputs
  //   Gate input enabler
  //   12sec Timer
  //   T
  //   I
  //   M
  //   E
  //   R
  //   Timer 12sec, Wait
  //   Fuel Normal now
  //   RUNWAY CHECKER AND ASSIGNER CIRCUIT
  //   T
  //   I
  //   M
  //   E
  //   R
  //   Input from Radar
  //   Pulse Generator
  //   00 - Low Fuel
  //   01 - Adequate Fuel
  //   10 - Adequate Fuel
  //   11 - High Fuel
  //   Fuel Quantity Calc.
  //   Pulse Generator
  //   Emergency Output
  //   Runway 0
  //   Filled
  //   Gate 0
  //   Ground Vehicles
  //   Dispatched
  //   GATE CHECKER AND ASSIGNER CIRCUIT
  //   Instructions
  //   Gate Allocation
  //   and Gates 4,5,6 are in terminal 2, next to runway 2
  //   1) Give the data in the radar first to implement landing
  //   2) Turn on take off signal first to implement the take off
  //   TEAM ID: T15
  //   Himanshu Singh Patel, 231CS127
  //   Nishant Kumar, 231CS140
  //   R Adithya, 231CS146
  //   Runway Allocation
  //   T
  //   I
  //   M
  //   E
  //   R
  //   Note that Gates 1,2,3 are in Terminal 1, next to runway 1.
  //   Also make sure the initial values of T flipflops are 0,0,0;
  //   3) The speed, range and altitude must reach an optimum level before the runway gets assigned
  //   4) Make sure to clear the series of T flip flops before using for ensuring correct outputs 
  //   REAL TIME AIR TRAFFIC CONTROL SYSTEM
  //   in case its not an emergency. Once its made optimum, the runway is assigned depending on other factors
  //   Runway Allocation
endmodule

module Pulse_gen (
  input  Radar_input,
  input  Radar_input_2,
  input  Clock,
  output Final_Pulse_Generator
);

  wire and_1_out, d_ff_1_q, d_ff_2_q, or_1_out;

  not not_1 (Final_Pulse_Generator, and_1_out);
  and and_1 (and_1_out, d_ff_1_q, or_1_out);
  D_Flip_Flop d_ff_1 (.clk(Clock), .D(d_ff_2_q), .Q(d_ff_1_q));  // open: Qn, preset, en, reset
  D_Flip_Flop d_ff_2 (.clk(Clock), .D(or_1_out), .Q(d_ff_2_q));  // open: Qn, preset, en, reset
  or or_1 (or_1_out, Radar_input, Radar_input_2);
endmodule

module Timer_12_final (
  input  Enable,
  input  Pulse_Generator,
  input  Clock,
  output A,
  output B,
  output C,
  output D,
  output Indicator
);

  wire and_1_out, and_2_out, not_1_out, not_2_out, not_3_out, not_4_out, not_5_out;

  not not_1 (not_1_out, and_1_out);
  and and_1 (and_1_out, not_2_out, not_3_out, not_4_out, not_5_out);
  and and_2 (and_2_out, Clock, not_1_out);
  J_K_Flip_Flop j_k_ff_1 (
    .J(1'b1), .clk(and_2_out), .K(1'b1), .Q(D), .en(Enable), .reset(Pulse_Generator));  // open: Qn, preset
  and and_3 (Indicator, not_2_out, not_3_out, not_4_out, not_5_out);
  not not_2 (not_2_out, D);
  not not_3 (not_3_out, C);
  not not_4 (not_4_out, B);
  not not_5 (not_5_out, A);
  J_K_Flip_Flop j_k_ff_2 (
    .J(1'b1), .clk(D), .K(1'b1), .Q(C), .en(Enable), .reset(Pulse_Generator));  // open: Qn, preset
  J_K_Flip_Flop j_k_ff_3 (
    .J(1'b1), .clk(C), .K(1'b1), .Q(B), .preset(Pulse_Generator), .en(Enable));  // open: Qn, reset
  J_K_Flip_Flop j_k_ff_4 (
    .J(1'b1), .clk(B), .K(1'b1), .Q(A), .preset(Pulse_Generator), .en(Enable));  // open: Qn, reset
endmodule

module Timer_15_final (
  input  Enable,
  input  Pulse_Generator,
  input  Clock,
  output A,
  output B,
  output C,
  output D,
  output Indicator
);

  wire and_1_out, and_2_out, not_1_out, not_2_out, not_3_out, not_4_out, not_5_out;

  not not_1 (not_1_out, and_1_out);
  and and_1 (and_1_out, not_2_out, not_3_out, not_4_out, not_5_out);
  and and_2 (and_2_out, Clock, not_1_out);
  J_K_Flip_Flop j_k_ff_1 (
    .J(1'b1), .clk(and_2_out), .K(1'b1), .Q(D), .preset(Pulse_Generator), .en(Enable));  // open: Qn, reset
  and and_3 (Indicator, not_5_out, not_4_out, not_3_out, not_2_out);
  not not_2 (not_2_out, D);
  not not_3 (not_3_out, C);
  not not_4 (not_4_out, B);
  not not_5 (not_5_out, A);
  J_K_Flip_Flop j_k_ff_2 (
    .J(1'b1), .clk(D), .K(1'b1), .Q(C), .preset(Pulse_Generator), .en(Enable));  // open: Qn, reset
  J_K_Flip_Flop j_k_ff_3 (
    .J(1'b1), .clk(C), .K(1'b1), .Q(B), .preset(Pulse_Generator), .en(Enable));  // open: Qn, reset
  J_K_Flip_Flop j_k_ff_4 (
    .J(1'b1), .clk(B), .K(1'b1), .Q(A), .preset(Pulse_Generator), .en(Enable));  // open: Qn, reset
endmodule

module Gate_to_Display (
  input  A,
  input  B,
  input  C,
  input  D,
  output a_2,
  output b_2,
  output c_2,
  output d_2,
  output e,
  output f,
  output g
);

  wire and_1_out, and_2_out, and_3_out, and_4_out, and_5_out, not_1_out, not_2_out, not_3_out, not_4_out,
       or_4_out;

  not not_1 (not_1_out, A);
  not not_2 (not_2_out, C);
  not not_3 (not_3_out, B);
  not not_4 (not_4_out, D);
  and and_1 (and_1_out, A, not_2_out);
  and and_2 (and_2_out, C, not_4_out);
  or or_1 (c_2, not_1_out, D, C);
  and and_3 (and_3_out, not_2_out, D);
  or or_2 (b_2, and_1_out, and_2_out);
  or or_3 (e, A, and_3_out);
  and and_4 (and_4_out, D, not_1_out);
  and and_5 (and_5_out, A, C);
  and and_6 (g, C, or_4_out);
  or or_4 (or_4_out, B, D);
  or or_5 (d_2, and_4_out, and_5_out);

  assign a_2 = B;
  assign f = B;
endmodule

module Custom_Comparator (
  input  A,
  input  B,
  input  C,
  output _3,
  output _3_2,
  output _0
);

  wire and_2_out, and_3_out, and_4_out, not_1_out, not_2_out, not_3_out;

  not not_1 (not_1_out, A);
  not not_2 (not_2_out, B);
  not not_3 (not_3_out, C);
  and and_1 (_0, not_1_out, not_2_out, not_3_out);
  and and_2 (and_2_out, not_1_out, C);
  and and_3 (and_3_out, not_1_out, B);
  and and_4 (and_4_out, B, C);
  or or_1 (_3_2, and_2_out, and_3_out, and_4_out);

  assign _3 = A;
endmodule
